// Logisim project circ.circ as structural Verilog: 1 circuit, main circuit main
module main (
);

  wire button_1_out, clock_1_out, comparator_1_eq, not_1_out, not_2_out, or_2_out, rgb_video_1_p1,
       rgb_video_1_p2;
  wire [1:0] register_1_q;
  wire [2:0] register_4_q, rgb_video_1_p5;
  wire [3:0] rom_1_data;
  wire [4:0] register_4_q_2, rgb_video_1_p5_2;
  wire [5:0] rgb_video_1_p4;
  wire [7:0] adder_1_out, and_2_out, button_9_out, controlled_buffer_1_out, counter_1_q, divider_1_out,
       multiplexer_1_out, multiplier_1_out, nand_1_out, nor_1_out, not_3_out, or_3_out, register_3_q,
       register_6_q, register_7_q, shifter_1_out, shifter_2_out, subtractor_1_out, xor_1_out;
  wire [9:0] counter_2_q;
  wire [15:0] ram_1_dout;
  wire [27:0] rom_1_data_2;

  // RGB_Video #(.cursor("No Cursor"), .height(64), .scale(6), .width(64)) rgb_video_1: pin names not known; wires that end beside it: rgb_video_1_p1, rgb_video_1_p2, rom_1_data_2[26], rgb_video_1_p4, {rgb_video_1_p5_2[2:0], rgb_video_1_p5}, {24{1'b1}}
  or or_1 (rgb_video_1_p1, button_1_out, rom_1_data_2[27]);
  assign controlled_buffer_1_out = rom_1_data_2[20] ? {register_1_q, rgb_video_1_p4} : 8'bz;  // Controlled_Buffer controlled_buffer_1
  Register register_1 (
    .D(controlled_buffer_1_out), .en(rom_1_data_2[24]), .Q({register_1_q, rgb_video_1_p4}),
    .clk(rgb_video_1_p2), .clr(button_1_out));
  Register register_2 (
    .D(controlled_buffer_1_out), .en(rom_1_data_2[23]), .Q({rgb_video_1_p5_2, rgb_video_1_p5}),
    .clk(rgb_video_1_p2), .clr(button_1_out));
  Register register_3 (
    .D(controlled_buffer_1_out), .en(rom_1_data_2[16]), .Q(register_3_q), .clk(rgb_video_1_p2),
    .clr(button_1_out));
  Button button_1 (.out(button_1_out));
  Button button_2 (.out(button_9_out[7]));
  Button button_3 (.out(button_9_out[6]));
  Button button_4 (.out(button_9_out[5]));
  assign controlled_buffer_1_out = rom_1_data_2[19] ? {rgb_video_1_p5_2, rgb_video_1_p5} : 8'bz;  // Controlled_Buffer controlled_buffer_2
  Register register_4 (
    .D(controlled_buffer_1_out), .en(rom_1_data_2[15]), .Q({register_4_q, register_4_q_2}),
    .clk(rgb_video_1_p2), .clr(button_1_out));
  Register #(.width(1)) register_5 (
    .D(comparator_1_eq), .en(rom_1_data_2[14]), .Q(counter_2_q[9]), .clk(rgb_video_1_p2), .clr(button_1_out));
  Button button_5 (.out(button_9_out[4]));
  Button button_6 (.out(button_9_out[3]));
  Button button_7 (.out(button_9_out[2]));
  Button button_8 (.out(button_9_out[1]));
  assign controlled_buffer_1_out = rom_1_data_2[18] ? register_6_q : 8'bz;  // Controlled_Buffer controlled_buffer_3
  Register register_6 (
    .D(controlled_buffer_1_out), .en(rom_1_data_2[22]), .Q(register_6_q), .clk(rgb_video_1_p2),
    .clr(button_1_out));
  assign controlled_buffer_1_out = rom_1_data_2[13] ? {8{1'b0}} : 8'bz;  // Controlled_Buffer controlled_buffer_4
  assign controlled_buffer_1_out = rom_1_data_2[10] ? counter_1_q : 8'bz;  // Controlled_Buffer controlled_buffer_5
  Counter counter_1 (
    .load(rom_1_data_2[11]), .D(controlled_buffer_1_out), .count(rom_1_data_2[9]), .Q(counter_1_q),
    .clk(rgb_video_1_p2), .clr(button_1_out));  // open: carry, up
  Clock clock_1 (.out(clock_1_out));
  not not_1 (not_1_out, button_1_out);
  Button button_9 (.out(button_9_out[0]));
  assign controlled_buffer_1_out = rom_1_data_2[25] ? button_9_out : 8'bz;  // Controlled_Buffer controlled_buffer_6
  assign controlled_buffer_1_out = rom_1_data_2[17] ? register_7_q : 8'bz;  // Controlled_Buffer controlled_buffer_7
  Register register_7 (
    .D(controlled_buffer_1_out), .en(rom_1_data_2[21]), .Q(register_7_q), .clk(rgb_video_1_p2),
    .clr(button_1_out));
  assign controlled_buffer_1_out = rom_1_data_2[12] ? 8'h1 : 8'bz;  // Controlled_Buffer controlled_buffer_8
  Counter #(.max('hf), .width(4)) counter_2 (
    .Q(counter_2_q[3:0]), .clk(not_2_out), .clr(or_2_out));  // open: load, D, count, carry, up
  not not_2 (not_2_out, rgb_video_1_p2);
  or or_2 (or_2_out, button_1_out, rom_1_data_2[8]);
  and and_1 (rgb_video_1_p2, clock_1_out, not_1_out);
  Comparator comparator_1 (
    .a({register_1_q, rgb_video_1_p4}), .b({rgb_video_1_p5_2, rgb_video_1_p5}), .eq(comparator_1_eq));  // open: gt, lt
  Adder adder_1 (
    .a({register_1_q, rgb_video_1_p4}), .b({rgb_video_1_p5_2, rgb_video_1_p5}), .out(adder_1_out));  // open: cin, cout
  Subtractor subtractor_1 (
    .a({register_1_q, rgb_video_1_p4}), .b({rgb_video_1_p5_2, rgb_video_1_p5}), .out(subtractor_1_out));  // open: bin, bout
  Multiplier multiplier_1 (
    .a({register_1_q, rgb_video_1_p4}), .b({rgb_video_1_p5_2, rgb_video_1_p5}), .out(multiplier_1_out));  // open: cin, cout
  Divider divider_1 (
    .a({register_1_q, rgb_video_1_p4}), .b({rgb_video_1_p5_2, rgb_video_1_p5}), .out(divider_1_out));  // open: upper, rem
  Shifter shifter_1 (.in({register_1_q, rgb_video_1_p4}), .\dist (rgb_video_1_p5), .out(shifter_1_out));
  Shifter #(.shift("lr")) shifter_2 (.in({register_1_q, rgb_video_1_p4}), .\dist (rgb_video_1_p5), .out(shifter_2_out));
  RAM #(.dataWidth(16), .enables("line")) ram_1 (
    .addr(register_3_q), .we(rom_1_data_2[2]), .clk(rgb_video_1_p2),
    .din({{8{1'b0}}, controlled_buffer_1_out}), .dout(ram_1_dout));
  ROM #(.addrWidth(10), .dataWidth(28)) rom_1 (
    .addr({counter_2_q[9], register_4_q_2, counter_2_q[3:0]}),
    .data({rom_1_data_2[27:8], rom_1_data, rom_1_data_2[3:0]}));
  Multiplexer #(.select(4), .width(8)) multiplexer_1 (
    .in0(adder_1_out), .in1(subtractor_1_out), .in2(multiplier_1_out), .in3(divider_1_out),
    .in4(shifter_1_out), .in5(shifter_2_out), .in6(not_3_out), .in7(and_2_out), .in8(or_3_out),
    .in9(nand_1_out), .in10(nor_1_out), .in11(xor_1_out), .out(multiplexer_1_out));  // open: in12, in13, in14, in15, sel
  assign controlled_buffer_1_out = rom_1_data_2[3] ? multiplexer_1_out : 8'bz;  // Controlled_Buffer controlled_buffer_9
  assign and_2_out = {register_1_q, rgb_video_1_p4} & {rgb_video_1_p5_2, rgb_video_1_p5};  // AND_Gate and_2, 8 bits wide
  assign or_3_out = {register_1_q, rgb_video_1_p4} | {rgb_video_1_p5_2, rgb_video_1_p5};  // OR_Gate or_3, 8 bits wide
  assign nand_1_out = ~({register_1_q, rgb_video_1_p4} & {rgb_video_1_p5_2, rgb_video_1_p5});  // NAND_Gate nand_1, 8 bits wide
  assign nor_1_out = ~({register_1_q, rgb_video_1_p4} | {rgb_video_1_p5_2, rgb_video_1_p5});  // NOR_Gate nor_1, 8 bits wide
  assign xor_1_out = {register_1_q, rgb_video_1_p4} ^ {rgb_video_1_p5_2, rgb_video_1_p5};  // XOR_Gate xor_1, 8 bits wide
  assign not_3_out = ~{register_1_q, rgb_video_1_p4};  // NOT_Gate not_3, 8 bits wide
  assign controlled_buffer_1_out = rom_1_data_2[0] ? ram_1_dout[7:0] : 8'bz;  // Controlled_Buffer controlled_buffer_10
  assign controlled_buffer_1_out = rom_1_data_2[1] ? ram_1_dout[15:8] : 8'bz;  // Controlled_Buffer controlled_buffer_11

  // Notes on the sheet:
  //   contents of rom_1 (hex, n*v repeats v):
  //   10400 8202 100 29*0 10400 8202 1000001 100 12*0 10400 8202 800001 100 12*0 10400 8202 10001 1000001
  //   100 11*0 10400 8202 10001 800001 100 11*0 10400 8202 10001 100004 100 11*0 10400 8202 10001 80004
  //   100 11*0 10400 8202 90000 1000001 100 11*0 10400 8202 90000 100004 100 11*0 10400 8202 8000000 100
  //   12*0 10400 8202 4000000 100 12*0 10400 8202 3000000 100 12*0 10400 8202 801000 1000008 100 11*0
  //   10400 8202 801000 1000018 100 11*0 10400 8202 10001 1000001 801000 1000008 100004 100 8*0 10400 8202
  //   10001 1000001 801000 1000018 100004 100 8*0 10400 8202 1004008 100 12*0 10400 8202 1004018 100 12*0
  //   10400 8202 1004028 100 12*0 10400 8202 1004038 100 12*0 10400 8202 1004048 100 12*0 10400 8202
  //   1004058 100 12*0 10400 8202 1004068 100 12*0 10400 8202 1004078 100 12*0 10400 8202 1004088 100 12*0
  //   10400 8202 1004098 100 12*0 10400 8202 10040a8 100 12*0 10400 8202 10040b8 100 12*0 10400 8202 4000
  //   100 12*0 10400 8202 801 100 12*0 10400 8202 100 13*0 10400 8202 100 29*0 10400 8202 1000001 100 12*0
  //   10400 8202 800001 100 12*0 10400 8202 10001 1000001 100 11*0 10400 8202 10001 800001 100 11*0 10400
  //   8202 10001 100004 100 11*0 10400 8202 10001 80004 100 11*0 10400 8202 90000 1000001 100 11*0 10400
  //   8202 90000 100004 100 11*0 10400 8202 8000000 100 12*0 10400 8202 4000000 100 12*0 10400 8202
  //   3000000 100 12*0 10400 8202 801000 1000008 100 11*0 10400 8202 801000 1000018 100 11*0 10400 8202
  //   10001 1000001 801000 1000008 100004 100 8*0 10400 8202 10001 1000001 801000 1000018 100004 100 8*0
  //   10400 8202 1004008 100 12*0 10400 8202 1004018 100 12*0 10400 8202 1004028 100 12*0 10400 8202
  //   1004038 100 12*0 10400 8202 1004048 100 12*0 10400 8202 1004058 100 12*0 10400 8202 1004068 100 12*0
  //   10400 8202 1004078 100 12*0 10400 8202 1004088 100 12*0 10400 8202 1004098 100 12*0 10400 8202
  //   10040a8 100 12*0 10400 8202 10040b8 100 12*0 10400 8202 4000 100 12*0 10400 8202 801 100 12*0 10400
  //   8202 801 100
endmodule
